# Fritzing sketch Fritzing (saved by Fritzing 0.9.3b)
circuit board: 5.27276cm x 5.07223cm
breadboards: 1

parts:
  Raspberry_Pi_1 = Raspberry Pi 3 [part_number=RPI-3-V1.2]
  SENSOR = Header 12 [package=1x12_machine-pin-header_lock.004]

nets:
  N1: Raspberry_Pi_1.3v3, SENSOR.2
  N2: Raspberry_Pi_1.GPIO2, SENSOR.5
  N3: Raspberry_Pi_1.GPIO3, SENSOR.4
  N4: Raspberry_Pi_1.GND, SENSOR.3, SENSOR.8
